// Logisim project 876768timing.circ as structural Verilog: 1 circuit, main circuit main
module main (
);

  wire buffer_16_out, buffer_23_out, buffer_27_out, buffer_36_out, H_BLANK, H_BP_BEG, H_BP_COM, H_BP_END,
       H_P_CLK, H_SP_BEG, H_SP_COM, H_SP_END, H_SYNC, HC_0, HC_1, HC_2, HC_3, HC_4, HC_5, HC_6, HC_7, HC_COM,
       not_9_out, not_13_out, not_20_out, not_23_out, O_P_CLK, P_CLK, V_BLANK, V_BP_BEG, V_BP_COM, V_BP_END,
       V_SP_BEG, V_SP_COM, V_SP_END, V_SYNC, VC_0, VC_1, VC_2, VC_3, VC_4, VC_5, VC_6, VC_7, VC_8, VC_9,
       VC_COM;

  Counter counter_1 (
    .Q({HC_7, HC_6, HC_5, HC_4, HC_3, HC_2, HC_1, HC_0}), .clk(P_CLK), .clr(H_BP_END));  // open: load, D, count, carry
  Clock clock_1 (.out(P_CLK));
  not not_1 (HC_COM, HC_7);
  Pull_Resistor pull_resistor_1 (.node(HC_COM));
  buf buffer_1 (H_BP_COM, HC_3);
  buf buffer_2 (H_BP_COM, HC_5);
  Pull_Resistor pull_resistor_2 (.node(H_BP_COM));
  buf buffer_3 (H_BP_COM, HC_COM);
  not not_2 (H_SP_COM, HC_0);
  buf buffer_4 (H_SP_COM, HC_6);
  buf buffer_5 (H_SP_COM, HC_COM);
  Pull_Resistor pull_resistor_3 (.node(H_SP_COM));
  Counter #(.width(10), .max('h3ff)) counter_2 (
    .Q({VC_9, VC_8, VC_7, VC_6, VC_5, VC_4, VC_3, VC_2, VC_1, VC_0}), .clk(H_BP_END), .clr(V_BP_END));  // open: load, D, count, carry
  buf buffer_6 (VC_COM, VC_1);
  buf buffer_7 (VC_COM, VC_4);
  buf buffer_8 (VC_COM, VC_6);
  buf buffer_9 (VC_COM, VC_7);
  not not_3 (VC_COM, VC_8);
  Pull_Resistor pull_resistor_4 (.node(VC_COM));
  not not_4 (VC_COM, VC_9);
  buf buffer_10 (V_BP_COM, VC_0);
  buf buffer_11 (V_BP_COM, VC_2);
  buf buffer_12 (V_BP_COM, VC_COM);
  Pull_Resistor pull_resistor_5 (.node(V_BP_COM));
  buf buffer_13 (V_SP_COM, VC_3);
  buf buffer_14 (V_SP_COM, VC_5);
  buf buffer_15 (V_SP_COM, VC_COM);
  Pull_Resistor pull_resistor_6 (.node(V_SP_COM));
  buf buffer_16 (buffer_16_out, HC_0);
  not not_5 (H_BP_BEG, buffer_16_out);
  not not_6 (buffer_16_out, HC_1);
  buf buffer_17 (buffer_16_out, HC_2);
  not not_7 (buffer_16_out, HC_4);
  buf buffer_18 (buffer_16_out, HC_6);
  buf buffer_19 (buffer_16_out, H_BP_COM);
  Pull_Resistor pull_resistor_7 (.node(buffer_16_out));
  not not_8 (H_BP_END, not_9_out);
  not not_9 (not_9_out, HC_0);
  buf buffer_20 (not_9_out, HC_1);
  not not_10 (not_9_out, HC_2);
  buf buffer_21 (not_9_out, HC_4);
  not not_11 (not_9_out, HC_6);
  buf buffer_22 (not_9_out, H_BP_COM);
  Pull_Resistor pull_resistor_8 (.node(not_9_out));
  S_R_Flip_Flop s_r_ff_1 (.Qn(H_BLANK), .preset(H_BP_BEG), .reset(H_BP_END));  // open: S, clk, R, Q, en
  and and_1 (H_P_CLK, H_BLANK, P_CLK);
  and and_2 (O_P_CLK, V_BLANK, H_P_CLK);
  buf buffer_23 (buffer_23_out, VC_3);
  not not_12 (V_BP_BEG, buffer_23_out);
  buf buffer_24 (buffer_23_out, VC_5);
  Pull_Resistor pull_resistor_9 (.node(buffer_23_out));
  buf buffer_25 (buffer_23_out, V_BP_COM);
  not not_13 (not_13_out, VC_3);
  not not_14 (V_BP_END, not_13_out);
  not not_15 (not_13_out, VC_5);
  Pull_Resistor pull_resistor_10 (.node(not_13_out));
  buf buffer_26 (not_13_out, V_BP_COM);
  S_R_Flip_Flop s_r_ff_2 (.Qn(V_BLANK), .preset(V_BP_BEG), .reset(V_BP_END));  // open: S, clk, R, Q, en
  not not_16 (H_SP_BEG, buffer_27_out);
  buf buffer_27 (buffer_27_out, HC_1);
  buf buffer_28 (buffer_27_out, HC_2);
  not not_17 (buffer_27_out, HC_3);
  not not_18 (buffer_27_out, HC_4);
  buf buffer_29 (buffer_27_out, HC_5);
  buf buffer_30 (buffer_27_out, H_SP_COM);
  Pull_Resistor pull_resistor_11 (.node(buffer_27_out));
  not not_19 (H_SP_END, not_20_out);
  not not_20 (not_20_out, HC_1);
  not not_21 (not_20_out, HC_2);
  buf buffer_31 (not_20_out, HC_3);
  buf buffer_32 (not_20_out, HC_4);
  not not_22 (not_20_out, HC_5);
  Pull_Resistor pull_resistor_12 (.node(not_20_out));
  buf buffer_33 (not_20_out, H_SP_COM);
  S_R_Flip_Flop s_r_ff_3 (.Qn(H_SYNC), .preset(H_SP_BEG), .reset(H_SP_END));  // open: S, clk, R, Q, en
  not not_23 (not_23_out, VC_0);
  buf buffer_34 (not_23_out, VC_2);
  buf buffer_35 (not_23_out, V_SP_COM);
  Pull_Resistor pull_resistor_13 (.node(not_23_out));
  buf buffer_36 (buffer_36_out, VC_0);
  not not_24 (buffer_36_out, VC_2);
  Pull_Resistor pull_resistor_14 (.node(buffer_36_out));
  buf buffer_37 (buffer_36_out, V_SP_COM);
  S_R_Flip_Flop s_r_ff_4 (.Qn(V_SYNC), .preset(V_SP_BEG), .reset(V_SP_END));  // open: S, clk, R, Q, en
  not not_25 (V_SP_BEG, not_23_out);
  not not_26 (V_SP_END, buffer_36_out);

  // Notes on the sheet:
  //   not_1 drives only 1 and floats otherwise
  //   buffer_1 drives only 1 and floats otherwise
  //   buffer_2 drives only 1 and floats otherwise
  //   buffer_3 drives only 1 and floats otherwise
  //   not_2 drives only 1 and floats otherwise
  //   buffer_4 drives only 1 and floats otherwise
  //   buffer_5 drives only 1 and floats otherwise
  //   buffer_6 drives only 1 and floats otherwise
  //   buffer_7 drives only 1 and floats otherwise
  //   buffer_8 drives only 1 and floats otherwise
  //   buffer_9 drives only 1 and floats otherwise
  //   not_3 drives only 1 and floats otherwise
  //   not_4 drives only 1 and floats otherwise
  //   buffer_10 drives only 1 and floats otherwise
  //   buffer_11 drives only 1 and floats otherwise
  //   buffer_12 drives only 1 and floats otherwise
  //   buffer_13 drives only 1 and floats otherwise
  //   buffer_14 drives only 1 and floats otherwise
  //   buffer_15 drives only 1 and floats otherwise
  //   buffer_16 drives only 1 and floats otherwise
  //   not_6 drives only 1 and floats otherwise
  //   buffer_17 drives only 1 and floats otherwise
  //   not_7 drives only 1 and floats otherwise
  //   buffer_18 drives only 1 and floats otherwise
  //   buffer_19 drives only 1 and floats otherwise
  //   not_9 drives only 1 and floats otherwise
  //   buffer_20 drives only 1 and floats otherwise
  //   not_10 drives only 1 and floats otherwise
  //   buffer_21 drives only 1 and floats otherwise
  //   not_11 drives only 1 and floats otherwise
  //   buffer_22 drives only 1 and floats otherwise
  //   buffer_23 drives only 1 and floats otherwise
  //   buffer_24 drives only 1 and floats otherwise
  //   buffer_25 drives only 1 and floats otherwise
  //   not_13 drives only 1 and floats otherwise
  //   not_15 drives only 1 and floats otherwise
  //   buffer_26 drives only 1 and floats otherwise
  //   buffer_27 drives only 1 and floats otherwise
  //   buffer_28 drives only 1 and floats otherwise
  //   not_17 drives only 1 and floats otherwise
  //   not_18 drives only 1 and floats otherwise
  //   buffer_29 drives only 1 and floats otherwise
  //   buffer_30 drives only 1 and floats otherwise
  //   not_20 drives only 1 and floats otherwise
  //   not_21 drives only 1 and floats otherwise
  //   buffer_31 drives only 1 and floats otherwise
  //   buffer_32 drives only 1 and floats otherwise
  //   not_22 drives only 1 and floats otherwise
  //   buffer_33 drives only 1 and floats otherwise
  //   not_23 drives only 1 and floats otherwise
  //   buffer_34 drives only 1 and floats otherwise
  //   buffer_35 drives only 1 and floats otherwise
  //   buffer_36 drives only 1 and floats otherwise
  //   not_24 drives only 1 and floats otherwise
  //   buffer_37 drives only 1 and floats otherwise
endmodule
